# Fritzing sketch Schematic (saved by Fritzing 0.9.3b)
breadboards: 1

parts:
  Part1 = Arduino Mega 2560 (Rev3)
  LED1 = RGB LED (com. cathode, rbg) [package="5 mm [THT]"]
  GY1 = MPU-6050 Board GY-521 [form="♀ (female)" package=THT]
  Part2 = Passive Buzzer

nets:
  N1: Part1.D21/SCL, GY1.pin3
  N2: Part1.D20/SDA, GY1.pin4
  N3: Part1.D13_PWM, LED1.blue_anode
  N4: Part1.D12_PWM, LED1.common_cathode
  N5: Part1.D11_PWM, LED1.red_anode
  N6: Part1.5V, GY1.pin1, Part2.S
  GND: Part1.GND, LED1.green_anode, GY1.pin2, Part2.GND
  N7: Part1.D7_PWM, Part2.NC

custom parts:
  MPU-6050 Board GY-521: Acelerometro y Giroscopio MPU-6050 Board GY-521
